// Logisim project circuiros 3.circ as structural Verilog
module add_1 (
  input  A,
  input  B,
  input  C,
  output S0,
  output S1,
  output S2,
  output S3,
  output S4,
  output S5,
  output S6,
  output S7
);

  wire not_1_out, not_2_out, not_3_out, not_4_out, not_5_out, not_6_out, not_7_out, not_8_out, not_9_out,
       not_10_out, not_11_out, not_12_out;

  not not_1 (not_1_out, A);
  not not_2 (not_2_out, A);
  not not_3 (not_3_out, A);
  not not_4 (not_4_out, A);
  not not_5 (not_5_out, B);
  not not_6 (not_6_out, B);
  not not_7 (not_7_out, B);
  not not_8 (not_8_out, B);
  not not_9 (not_9_out, C);
  not not_10 (not_10_out, C);
  not not_11 (not_11_out, C);
  not not_12 (not_12_out, C);
  and and_1 (S0, not_1_out, not_5_out, not_9_out);
  and and_2 (S1, not_2_out, not_6_out, C);
  and and_3 (S2, not_3_out, B, not_10_out);
  and and_4 (S3, not_4_out, B, C);
  and and_5 (S4, A, not_7_out, not_11_out);
  and and_6 (S5, A, not_8_out, C);
  and and_7 (S6, A, B, not_12_out);
  and and_8 (S7, A, B, C);
endmodule
