// Logisim project circuito 4 bits 2.0.circ as structural Verilog: 3 circuits, main circuit main
module main (
  input  [3:0] in_1,
  input  [3:0] in_2,
  output out_3,
  output [3:0] out_4
);

  // Probe on in_1
  add_4 add_4_1 (.A(in_1), .out_3(out_3), .B(in_2), .out_4(out_4));
  // Probe on out_4
  // Probe on in_2
endmodule

module add1 (
  input  A,
  input  B,
  input  C,
  output S,
  output vai1
);

  wire and_1_out, and_2_out, and_3_out, and_4_out, and_5_out, and_6_out, and_7_out, and_8_out;

  and and_1 (and_1_out, ~A, ~B, C);  // AND_Gate
  and and_2 (and_2_out, ~A, B, ~C);  // AND_Gate
  and and_3 (and_3_out, A, ~B, ~C);  // AND_Gate
  and and_4 (and_4_out, A, B, C);
  and and_5 (and_5_out, ~A, B, C);  // AND_Gate
  and and_6 (and_6_out, A, ~B, C);  // AND_Gate
  and and_7 (and_7_out, A, B, ~C);  // AND_Gate
  and and_8 (and_8_out, A, B, C);
  or or_1 (S, and_1_out, and_2_out, and_3_out, and_4_out);
  or or_2 (vai1, and_5_out, and_6_out, and_7_out, and_8_out);
endmodule

module add_4 (
  input  [3:0] B,
  input  [3:0] A,
  output out_3,
  output [3:0] out_4
);

  wire add1_1_vai1, add1_3_vai1, add1_4_vai1;

  // Probe on A
  add1 add1_1 (.S(out_4[2]), .vai1(add1_1_vai1), .A(B[2]), .B(A[2]), .C(add1_3_vai1));
  add1 add1_2 (.S(out_4[3]), .vai1(out_3), .A(B[3]), .B(A[3]), .C(add1_1_vai1));
  add1 add1_3 (.S(out_4[1]), .vai1(add1_3_vai1), .A(B[1]), .B(A[1]), .C(add1_4_vai1));
  // Probe on out_4
  add1 add1_4 (.S(out_4[0]), .vai1(add1_4_vai1), .A(B[0]), .B(A[0]), .C(1'b0));
  // Probe on B
endmodule
