// Logisim project circuitos.circ as structural Verilog: 3 circuits, main circuit main
module main (
  input  [3:0] in_1,
  input  [3:0] in_2,
  output out_3,
  output [3:0] out_4
);

  // Probe on in_1
  add4 add4_1 (.in_2(in_1), .in_1(in_2), .in_3(1'b0), .out_5(out_4), .out_4(out_3));
  // Probe on in_2
  // Probe on out_4
endmodule

module add (
  input  a,
  input  b,
  input  in_3,
  output out_4,
  output out_5
);

  wire and_1_out, and_2_out, and_3_out, xor_1_out;

  xor xor_1 (xor_1_out, a, b);
  and and_1 (and_1_out, a, in_3);
  and and_2 (and_2_out, a, b);
  and and_3 (and_3_out, b, in_3);
  xor xor_2 (out_4, xor_1_out, in_3);
  or or_1 (out_5, and_1_out, and_2_out, and_3_out);

  // Notes on the sheet:
  //   c
endmodule

module add4 (
  input  [3:0] in_1,
  input  [3:0] in_2,
  input  in_3,
  output out_4,
  output [3:0] out_5
);

  wire add_2_out_5, add_3_out_5, add_4_out_5;

  // Probe on in_2
  add add_1 (.a(in_1[3]), .b(in_2[3]), .in_3(add_3_out_5), .out_4(out_5[3]), .out_5(out_4));
  // Probe on in_1
  add add_2 (.a(in_1[1]), .b(in_2[1]), .in_3(add_4_out_5), .out_4(out_5[1]), .out_5(add_2_out_5));
  add add_3 (.a(in_1[2]), .b(in_2[2]), .in_3(add_2_out_5), .out_4(out_5[2]), .out_5(add_3_out_5));
  // Probe on out_5
  add add_4 (.a(in_1[0]), .b(in_2[0]), .in_3(in_3), .out_4(out_5[0]), .out_5(add_4_out_5));

  // Notes on the sheet:
  //   add
endmodule
