// Logisim project circuitos_contador.circ as structural Verilog: 2 circuits, main circuit main
module main (
  input  A,
  input  B,
  input  C,
  output A_2,
  output B_2,
  output C_2,
  output D,
  output E,
  output F,
  output G
);

  and and_1 (G, ~A, ~B);  // AND_Gate
  or or_1 (B_2, B, ~C);  // OR_Gate
  or or_2 (D, A, C);
  or or_3 (E, C, ~B);  // OR_Gate
  or or_4 (A_2, G, C);

  assign C_2 = B_2;
  assign F = E;
endmodule

module add2 (
  input  in_1,
  input  in_2,
  input  in_3
);

  wire clock_1_out, main_1_a_2, main_1_b_2, main_1_c_2, main_1_d, main_1_e, main_1_f, main_1_g, main_2_a_2,
       main_2_b_2, main_2_c_2, main_2_d, main_2_e, main_2_f, main_2_g;
  wire [2:0] counter_1_q;

  main main_1 (
    .A_2(main_1_a_2), .B_2(main_1_b_2), .C_2(main_1_c_2), .D(main_1_d), .E(main_1_e), .F(main_1_f),
    .G(main_1_g), .A(in_1), .B(in_2), .C(in_3));
  _7_Segment_Display u_7_segment_display_1 (
    .g(main_1_g), .f(main_1_f), .a(main_1_a_2), .b(main_1_b_2), .e(main_1_e), .d(main_1_d), .c(main_1_c_2));  // open: dp
  Counter #(.width(3), .max('h4), .ongoal("continue")) counter_1 (
    .Q(counter_1_q), .clk(clock_1_out));  // open: load, D, count, carry, clr
  Clock clock_1 (.out(clock_1_out));
  main main_2 (
    .A_2(main_2_a_2), .B_2(main_2_b_2), .C_2(main_2_c_2), .D(main_2_d), .E(main_2_e), .F(main_2_f),
    .G(main_2_g), .A(counter_1_q[2]), .B(counter_1_q[1]), .C(counter_1_q[0]));
  _7_Segment_Display u_7_segment_display_2 (
    .g(main_2_g), .f(main_2_f), .a(main_2_a_2), .b(main_2_b_2), .e(main_2_e), .d(main_2_d), .c(main_2_c_2));  // open: dp
endmodule
