// Logisim project exemplo1.circ as structural Verilog: 3 circuits, main circuit main
module main (
  input  in_1,
  input  in_2,
  input  in_3,
  input  in_4,
  input  in_5,
  input  in_6,
  output out_7,
  output out_8
);

  exemplo2 exemplo2_1 (.in_1(in_4), .in_2(in_5), .in_3(in_6), .out_4(out_8));
  macro macro_1 (.A(in_1), .B(in_2), .C(in_3), .S(out_7));
endmodule

module macro (
  input  A,
  input  B,
  input  C,
  output S
);

  wire not_1_out, not_2_out, or_1_out, xor_1_out;

  xor xor_1 (xor_1_out, A, B);
  not not_1 (not_1_out, A);
  or or_1 (or_1_out, xor_1_out, not_1_out);
  not not_2 (not_2_out, C);
  and and_1 (S, or_1_out, not_2_out);
endmodule

module exemplo2 (
  input  in_1,
  input  in_2,
  input  in_3,
  output out_4
);

  wire and_1_out, not_1_out, not_2_out, not_3_out, or_1_out, xor_1_out;

  xor xor_1 (xor_1_out, in_1, in_2);
  not not_1 (not_1_out, in_2);
  or or_1 (or_1_out, xor_1_out, not_1_out);
  not not_2 (not_2_out, in_1);
  and and_1 (and_1_out, or_1_out, not_2_out);
  not not_3 (not_3_out, in_3);
  or or_2 (out_4, and_1_out, not_3_out);
endmodule
